# Fritzing sketch hidden_device (saved by Fritzing 1.0.0rc)
breadboards: 2

parts:
  FSR = Basic Force Sensing Resistor (FSR) [package=THT]
  U1 = ESP8266 ESP-01 Upgraded WiFi Module [part_number=.]
  R1 = Resistor [tolerance=±5% power=0.25W resistance=10k package=THT]
  R2 = Resistor [tolerance=±5% power=0.25W resistance=10k package=THT]
  R3 = Resistor [tolerance=±5% power=0.25W resistance=10k package=THT]
  Buzzer = Piezo Speaker
  R4 = Resistor [tolerance=±5% power=0.25W resistance=220 package=THT]
  Mod1 = KY-019 5V Relay Module [package="Breakout board"]
  U2 = DFRobot SEN0030 [package=THT]
  VCC1 = Battery block 9V
  R5 = Resistor [tolerance=±5% power=0.25W resistance=10k part_number=. package=THT]
  Componente2 = Arduino Uno Mini LE
  U3 = DFRobot 0021-G [package=THT]
  R6 = Resistor [tolerance=±5% power=0.25W resistance=470 package=THT]
  R7 = Resistor [tolerance=±5% power=0.25W resistance=470 package=THT]
  R8 = Resistor [tolerance=±5% power=0.25W resistance=680 package=THT]
  VCC2 = Battery 5V
  110_dB1 = Siren 110dB

nets:
  N1: FSR.pin_1, R5.Pin_0, Componente2.A0
  VCC: FSR.pin_2, U1.VCC, U1.CH_PD, Mod1.+, U2.P1_2, Componente2.3V3
  N2: U1.RXD, R2.Pin_1, R3.Pin_0
  GND: U1.GND, R1.Pin_0, Buzzer.pin1, Mod1.-, U2.P1_3, R5.Pin_1, Componente2.GND, VCC2.-
  N3: U1.TXD, Componente2.D3_PWM
  N4: R1.Pin_1, R2.Pin_0
  N5: R3.Pin_1, Componente2.D5_PWM
  N6: Buzzer.pin2, R4.Pin_1
  N7: R4.Pin_0, Componente2.D13/SCK
  N8: Mod1.S, Componente2.D9_PWM
  N9: Mod1.NC, 110_dB1.pin2
  N10: Mod1.Common, VCC1.+, R6.Pin_0
  N11: U2.P1_1, Componente2.D11_PWM/MOSI
  N12: VCC1.-, U3.P1_3, R8.Pin_1, 110_dB1.pin1
  N13: Componente2.D7, Componente2.RESET
  N14: Componente2.VIN, VCC2.+
  N15: U3.P1_2, R7.Pin_1, R8.Pin_0
  N16: R6.Pin_1, R7.Pin_0

custom parts:
  ESP8266 ESP-01 Upgraded WiFi Module: Upgraded Version ESP-01,all Flash are upgraded to 1M byte.Also support Cloud service remote transmission.
  KY-019 5V Relay Module: KY-019 5V Relay module, used to control AC circuits. (Special thanks to vanepp for fixing the PCB holes and other errors)
  DFRobot SEN0030: DFRobot Capacitive Touch Sensor SKU DFR0030
  Arduino Uno Mini LE: The UNO Mini Limited Edition (LE) is a miniature version of the classic Arduino UNO board. It is based on the ATmega328P microcontroller, has USB-C connector for programming and powering the board, and pins available for connecting external power sources. It also comes with the standard set of female pin connectors, built-in LED, reset button and everything else that the standard UNO have, but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
  DFRobot 0021-G: DFRobot Gravity: Digital Green LED Light Module
  Battery 5V: Duracell PB 6700
  Siren 110dB: Siren 110 dB
